// Digital circuit cpu.dig as structural Verilog
module cpu (
  input  clk
);

  wire clear_out, register_16bits_1_ovf;
  wire [3:0] load_out;
  wire [15:0] register_16bits_1_ival;

  DipSwitch load (.out(load_out[0]));
  DipSwitch enabled (.out(load_out[1]));
  DipSwitch count (.out(load_out[2]));
  DipSwitch direction (.out(load_out[3]));
  DipSwitch clear (.out(clear_out));
  LED led_1 (.in(register_16bits_1_ival[15]));
  LED led_2 (.in(register_16bits_1_ival[14]));
  register_16bits register_16bits_1 (
    .in({16{1'b1}}), .clk(clk), .ctrl(load_out), .clr(clear_out), .ival(register_16bits_1_ival),
    .ovf(register_16bits_1_ovf));  // open: out
  LED led_3 (.in(register_16bits_1_ival[13]));
  LED led_4 (.in(register_16bits_1_ival[12]));
  LED led_5 (.in(register_16bits_1_ival[11]));
  LED led_6 (.in(register_16bits_1_ival[10]));
  LED led_7 (.in(register_16bits_1_ival[9]));
  LED led_8 (.in(register_16bits_1_ival[8]));
  LED led_9 (.in(register_16bits_1_ival[7]));
  LED led_10 (.in(register_16bits_1_ival[6]));
  LED led_11 (.in(register_16bits_1_ival[5]));
  LED led_12 (.in(register_16bits_1_ival[4]));
  LED led_13 (.in(register_16bits_1_ival[3]));
  LED led_14 (.in(register_16bits_1_ival[2]));
  LED led_15 (.in(register_16bits_1_ovf));
  LED led_16 (.in(register_16bits_1_ival[1]));
  LED led_17 (.in(register_16bits_1_ival[0]));
endmodule
